# Fritzing sketch diagram (saved by Fritzing 0.9.9b)
breadboards: 1

parts:
  Mod2 = KY-005 Infrared Transmitter Module [package="Breakout board"]
  U1 = NodeMCU V1.0

nets:
  N1: Mod2.S, U1.D8
  VIN: Mod2.Vin, U1.3V3
  N2: Mod2.-, U1.GND

custom parts:
  KY-005 Infrared Transmitter Module: Arduino IR Transmitter Module Keyes KY-005, emits infrared light at 38KHz.
  NodeMCU V1.0: ESP8266 based NodeMCU
